// Digital circuit RV32I-Decode-Control.dig as structural Verilog
module RV32I_Decode_Control (
  input  [31:0] INSTR,
  input  Normal,
  input  Run,
  input  Go,
  output DECODE_HOLD,
  output DECODE_EN,
  output RESERVE,
  output ERROR
);

  wire rv32i_instruction_decoder_1_p3, rv32i_instruction_decoder_1_p4;

  // RV32I_Instruction_Decoder rv32i_instruction_decoder_1: pin names not known; wires that end beside it: INSTR, DECODE_HOLD, rv32i_instruction_decoder_1_p3, rv32i_instruction_decoder_1_p4
  and and_1 (DECODE_EN, Normal, Run);
  and and_2 (RESERVE, rv32i_instruction_decoder_1_p3, Normal, Run, Go);
  and and_3 (ERROR, rv32i_instruction_decoder_1_p4, Run, Normal, Go);
endmodule
