// Digital circuit RV32I-Execute-Control.dig as structural Verilog
module RV32I_Execute_Control (
  input  [31:0] INSTR,
  input  Normal,
  input  Run,
  output EXECUTE_HOLD,
  output EXECUTE_EN,
  output [7:0] ALU_INSTR,
  output [7:0] COMP_SEL,
  output [4:0] RS1_A,
  output [4:0] RS2_A
);

  // RV32I_Instruction_Decoder rv32i_instruction_decoder_1: pin names not known; wires that end beside it: INSTR, ALU_INSTR, COMP_SEL
  and and_1 (EXECUTE_HOLD, ~INSTR[4], INSTR[5], INSTR[6]);  // And
  and and_2 (EXECUTE_EN, Normal, Run);

  assign RS1_A = INSTR[19:15];
  assign RS2_A = INSTR[24:20];
endmodule
